// Logisim project espinosaJ.circ as structural Verilog
module CPU_MEM_1 (
  input  s,
  input  e,
  output q
);

  wire nand_1_out, nand_2_out, nand_4_out;

  nand nand_1 (nand_1_out, s, e);
  nand nand_2 (nand_2_out, nand_1_out, e);
  nand nand_3 (q, nand_1_out, nand_4_out);
  nand nand_4 (nand_4_out, q, nand_2_out);

  // Notes on the sheet:
  //   Component of 8 bit memory cell
  //   Jake Espinosa
  //   CS306
  //   Study.com
  //   1 bit memory cell
endmodule

module CPU_MEM_8 (
  input  [7:0] in_1,
  input  s,
  output [7:0] out_3
);

  CPU_MEM_1 cpu_mem_1_1 (.s(in_1[0]), .e(s), .q(out_3[0]));
  CPU_MEM_1 cpu_mem_1_2 (.s(in_1[1]), .e(s), .q(out_3[1]));
  CPU_MEM_1 cpu_mem_1_3 (.s(in_1[2]), .e(s), .q(out_3[2]));
  CPU_MEM_1 cpu_mem_1_4 (.s(in_1[3]), .e(s), .q(out_3[3]));
  CPU_MEM_1 cpu_mem_1_5 (.s(in_1[4]), .e(s), .q(out_3[4]));
  CPU_MEM_1 cpu_mem_1_6 (.s(in_1[5]), .e(s), .q(out_3[5]));
  CPU_MEM_1 cpu_mem_1_7 (.s(in_1[6]), .e(s), .q(out_3[6]));
  CPU_MEM_1 cpu_mem_1_8 (.s(in_1[7]), .e(s), .q(out_3[7]));

  // Notes on the sheet:
  //   Component of 8 bit register
  //   Jake Espinosa
  //   CS306
  //   Study.com
endmodule

module CPU_ENABLE (
  input  [7:0] in_1,
  input  e,
  output [7:0] out_3
);

  and and_1 (out_3[0], in_1[0], e);
  and and_2 (out_3[1], in_1[1], e);
  and and_3 (out_3[2], in_1[2], e);
  and and_4 (out_3[3], in_1[3], e);
  and and_5 (out_3[4], in_1[4], e);
  and and_6 (out_3[5], in_1[5], e);
  and and_7 (out_3[6], in_1[6], e);
  and and_8 (out_3[7], in_1[7], e);

  // Notes on the sheet:
  //   Jake Espinosa
  //   Study.com
  //   Component of 8 bit register
  //   CS306
  //   i
  //   o
endmodule

module CPU_REG_8 (
  input  [7:0] in_1,
  input  s,
  input  e,
  output [7:0] out_4
);

  wire [7:0] cpu_mem_8_1_out_3;

  CPU_MEM_8 cpu_mem_8_1 (.in_1(in_1), .out_3(cpu_mem_8_1_out_3), .s(s));
  CPU_ENABLE cpu_enable_1 (.in_1(cpu_mem_8_1_out_3), .out_3(out_4), .e(e));

  // Notes on the sheet:
  //   8 Bit Register
  //   Jake Espinosa
  //   CS306
  //   Study.com
endmodule

module halfAdder (
  input  A,
  input  B,
  output Sum,
  output Carry
);

  and and_1 (Carry, A, B);
  xor xor_1 (Sum, A, B);

  // Notes on the sheet:
  //   Half Adder
  //   Jake Espinosa
  //   CS306
  //   Study.com
endmodule

module fullAdder (
  input  A,
  input  B,
  input  Ci,
  output Sum,
  output Carry
);

  wire halfadder_1_carry, halfadder_1_sum, halfadder_2_carry;

  halfAdder halfadder_1 (.A(A), .B(B), .Sum(halfadder_1_sum), .Carry(halfadder_1_carry));
  halfAdder halfadder_2 (.A(halfadder_1_sum), .B(Ci), .Sum(Sum), .Carry(halfadder_2_carry));
  or or_1 (Carry, halfadder_2_carry, halfadder_1_carry);

  // Notes on the sheet:
  //   Full Adder
  //   Jake Espinosa
  //   CS306
  //   Study.com
endmodule

module arithmeticAddition (
  input  [7:0] in_1,
  input  [7:0] in_2,
  input  carry_in,
  output carry_out,
  output [7:0] out_5
);

  wire fulladder_2_carry, fulladder_3_carry, fulladder_4_carry, fulladder_5_carry, fulladder_6_carry,
       fulladder_7_carry, fulladder_8_carry;

  fullAdder fulladder_1 (.A(in_1[7]), .B(in_2[7]), .Ci(fulladder_2_carry), .Sum(out_5[7]), .Carry(carry_out));
  fullAdder fulladder_2 (.A(in_1[6]), .B(in_2[6]), .Ci(fulladder_3_carry), .Sum(out_5[6]), .Carry(fulladder_2_carry));
  fullAdder fulladder_3 (.A(in_1[5]), .B(in_2[5]), .Ci(fulladder_4_carry), .Sum(out_5[5]), .Carry(fulladder_3_carry));
  fullAdder fulladder_4 (.A(in_1[4]), .B(in_2[4]), .Ci(fulladder_5_carry), .Sum(out_5[4]), .Carry(fulladder_4_carry));
  fullAdder fulladder_5 (.A(in_1[3]), .B(in_2[3]), .Ci(fulladder_6_carry), .Sum(out_5[3]), .Carry(fulladder_5_carry));
  fullAdder fulladder_6 (.A(in_1[2]), .B(in_2[2]), .Ci(fulladder_7_carry), .Sum(out_5[2]), .Carry(fulladder_6_carry));
  fullAdder fulladder_7 (.A(in_1[1]), .B(in_2[1]), .Ci(fulladder_8_carry), .Sum(out_5[1]), .Carry(fulladder_7_carry));
  fullAdder fulladder_8 (.A(in_1[0]), .B(in_2[0]), .Ci(carry_in), .Sum(out_5[0]), .Carry(fulladder_8_carry));

  // Notes on the sheet:
  //   Arithmetic Addition
  //   Jake Espinosa
  //   CS306
  //   Study.com
  //   a
  //   b
endmodule

module _8BitRegister (
  input  [7:0] in_1,
  input  s,
  input  e,
  output [7:0] REG,
  output [7:0] out_5
);

  wire [7:0] cpu_mem_8_2_out_3;

  CPU_MEM_8 cpu_mem_8_1 (.in_1(in_1), .out_3(REG), .s(s));
  CPU_MEM_8 cpu_mem_8_2 (.in_1(REG), .out_3(cpu_mem_8_2_out_3), .s(e));
  assign out_5 = e ? cpu_mem_8_2_out_3 : 8'bz;  // Controlled_Buffer controlled_buffer_1

  // Notes on the sheet:
  //   i
  //   8-Bit Register
  //   Jake Espinosa
  //   CS306
  //   Study.com
  //   o
endmodule

module registerLeftLogicShift (
  input  [7:0] in_1,
  output shift_in,
  output [7:0] out_3,
  output shift_out
);

  wire [6:0] n8bitregister_1_out_5;

  _8BitRegister u_8bitregister_1 (
    .in_1(in_1), .s(1'b1), .e(1'b1), .out_5({shift_out, n8bitregister_1_out_5}));  // open: REG
  _8BitRegister u_8bitregister_2 (
    .in_1({n8bitregister_1_out_5, shift_in}), .s(1'b1), .e(1'b1), .out_5(out_3));  // open: REG

  // Notes on the sheet:
  //   i
  //   Shift Left
  //   Jake Espinosa
  //   CS306
  //   Study.com
  //   o
endmodule

module registerRightLogicShift (
  input  [7:0] in_1,
  input  shift_in,
  output shift_out,
  output [7:0] out_4
);

  wire [7:1] n8bitregister_1_out_5;

  _8BitRegister u_8bitregister_1 (
    .in_1(in_1), .s(1'b1), .e(1'b1), .out_5({n8bitregister_1_out_5, shift_out}));  // open: REG
  _8BitRegister u_8bitregister_2 (
    .in_1({shift_in, n8bitregister_1_out_5}), .s(1'b1), .e(1'b1), .out_5(out_4));  // open: REG

  // Notes on the sheet:
  //   i
  //   Shift Right
  //   Jake Espinosa
  //   CS306
  //   Study.com
  //   o
endmodule

module logicBitwiseNOT (
  input  [7:0] in_1,
  output [7:0] out_2
);

  not not_1 (out_2[0], in_1[0]);
  not not_2 (out_2[1], in_1[1]);
  not not_3 (out_2[2], in_1[2]);
  not not_4 (out_2[3], in_1[3]);
  not not_5 (out_2[4], in_1[4]);
  not not_6 (out_2[5], in_1[5]);
  not not_7 (out_2[6], in_1[6]);
  not not_8 (out_2[7], in_1[7]);

  // Notes on the sheet:
  //   i
  //   Logic Bitwise NOT
  //   Jake Espinosa
  //   CS306
  //   Study.com
  //   o
endmodule

module logicBitwiseAND (
  input  [7:0] in_1,
  input  [7:0] in_2,
  output [7:0] out_3
);

  and and_1 (out_3[0], in_1[0], in_2[0]);
  and and_2 (out_3[1], in_1[1], in_2[1]);
  and and_3 (out_3[2], in_1[2], in_2[2]);
  and and_4 (out_3[3], in_1[3], in_2[3]);
  and and_5 (out_3[4], in_1[4], in_2[4]);
  and and_6 (out_3[5], in_1[5], in_2[5]);
  and and_7 (out_3[6], in_1[6], in_2[6]);
  and and_8 (out_3[7], in_1[7], in_2[7]);

  // Notes on the sheet:
  //   a
  //   b
  //   Logic Bitwise AND
  //   Jake Espinosa
  //   CS306
  //   Study.com
  //   o
endmodule

module logicBitwiseOR (
  input  [7:0] in_1,
  input  [7:0] in_2,
  output [7:0] out_3
);

  or or_1 (out_3[0], in_1[0], in_2[0]);
  or or_2 (out_3[1], in_1[1], in_2[1]);
  or or_3 (out_3[2], in_1[2], in_2[2]);
  or or_4 (out_3[3], in_1[3], in_2[3]);
  or or_5 (out_3[4], in_1[4], in_2[4]);
  or or_6 (out_3[5], in_1[5], in_2[5]);
  or or_7 (out_3[6], in_1[6], in_2[6]);
  or or_8 (out_3[7], in_1[7], in_2[7]);

  // Notes on the sheet:
  //   Logic Bitwise OR
  //   Jake Espinosa
  //   CS306
  //   Study.com
  //   a
  //   b
  //   o
endmodule

module componentOfComparison (
  input  above_equal,
  input  a_larger,
  input  a,
  input  b,
  output c,
  output equal,
  output a_large
);

  wire and_2_out, not_1_out;

  // CPU_XOR_1 cpu_xor_1_1: pin names not known; wires that end beside it: a, b, c, above_equal
  not not_1 (not_1_out, c);
  and and_1 (equal, not_1_out, above_equal);
  and and_2 (and_2_out, above_equal, a, c);
  or or_1 (a_large, and_2_out, a_larger);

  // Notes on the sheet:
  //   Component of Comparison
  //   Jake Espinosa
  //   CS306
  //   Study.com
endmodule

module comparison (
  input  [7:0] a,
  input  [7:0] b,
  output [7:0] out_3,
  output a___b,
  output a____b,
  output a___b_2
);

  wire cpu_xor_le_1_1_p4, cpu_xor_le_1_1_p6, cpu_xor_le_1_2_p4, cpu_xor_le_1_2_p6, cpu_xor_le_1_3_p4,
       cpu_xor_le_1_3_p6, cpu_xor_le_1_4_p4, cpu_xor_le_1_4_p6, cpu_xor_le_1_5_p4, cpu_xor_le_1_5_p6,
       cpu_xor_le_1_6_p4, cpu_xor_le_1_6_p6, cpu_xor_le_1_7_p4, cpu_xor_le_1_7_p6, not_1_out, not_2_out;

  // CPU_XOR_LE_1 cpu_xor_le_1_1: pin names not known; wires that end beside it: a[7], b[7], 1'b1, cpu_xor_le_1_1_p4, 1'b0, cpu_xor_le_1_1_p6, out_3[7]
  // CPU_XOR_LE_1 cpu_xor_le_1_2: pin names not known; wires that end beside it: a[6], b[6], cpu_xor_le_1_1_p4, cpu_xor_le_1_2_p4, cpu_xor_le_1_1_p6, cpu_xor_le_1_2_p6, out_3[6]
  // CPU_XOR_LE_1 cpu_xor_le_1_3: pin names not known; wires that end beside it: a[5], b[5], cpu_xor_le_1_2_p4, cpu_xor_le_1_3_p4, cpu_xor_le_1_2_p6, cpu_xor_le_1_3_p6, out_3[5]
  // CPU_XOR_LE_1 cpu_xor_le_1_4: pin names not known; wires that end beside it: a[4], b[4], cpu_xor_le_1_3_p4, cpu_xor_le_1_4_p4, cpu_xor_le_1_3_p6, cpu_xor_le_1_4_p6, out_3[4]
  // CPU_XOR_LE_1 cpu_xor_le_1_5: pin names not known; wires that end beside it: a[3], b[3], cpu_xor_le_1_4_p4, cpu_xor_le_1_5_p4, cpu_xor_le_1_4_p6, cpu_xor_le_1_5_p6, out_3[3]
  // CPU_XOR_LE_1 cpu_xor_le_1_6: pin names not known; wires that end beside it: a[2], b[2], cpu_xor_le_1_5_p4, cpu_xor_le_1_6_p4, cpu_xor_le_1_5_p6, cpu_xor_le_1_6_p6, out_3[2]
  // CPU_XOR_LE_1 cpu_xor_le_1_7: pin names not known; wires that end beside it: a[1], b[1], cpu_xor_le_1_6_p4, cpu_xor_le_1_7_p4, cpu_xor_le_1_6_p6, cpu_xor_le_1_7_p6, out_3[1]
  // CPU_XOR_LE_1 cpu_xor_le_1_8: pin names not known; wires that end beside it: a[0], b[0], cpu_xor_le_1_7_p4, a____b, cpu_xor_le_1_7_p6, a___b, out_3[0]
  not not_1 (not_1_out, a___b);
  not not_2 (not_2_out, a____b);
  and and_1 (a___b_2, not_1_out, not_2_out);

  // Notes on the sheet:
  //   Comparison
  //   Jake Espinosa
  //   CS306
  //   Study.com
endmodule

module increment (
  input  [7:0] in_1,
  input  in_2,
  output out_3,
  output [7:0] out_4
);

  arithmeticAddition arithmeticaddition_1 (.in_1(8'h1), .in_2(in_1), .out_5(out_4), .carry_out(out_3), .carry_in(in_2));

  // Notes on the sheet:
  //   Incrementer
  //   Jake Espinosa
  //   CS306
  //   Study.com
endmodule

module decrement (
  input  [7:0] in_1,
  input  in_2,
  output out_3,
  output [7:0] out_4
);

  arithmeticAddition arithmeticaddition_1 (
    .in_1({8{1'b1}}), .in_2(in_1), .out_5(out_4), .carry_out(out_3), .carry_in(in_2));

  // Notes on the sheet:
  //   Decrementer
  //   Jake Espinosa
  //   CS306
  //   Study.com
endmodule

module phase3 (
  input  [7:0] in_1,
  input  [7:0] in_2,
  input  [7:0] in_3,
  input  in_4,
  input  in_5,
  input  in_6,
  input  in_7,
  output [7:0] out_8
);

  wire and_1_out, and_2_out, and_3_out;
  wire [7:0] arithmeticaddition_1_out_5, cpu_enable_1_out_3, cpu_enable_2_out_3, cpu_enable_3_out_3,
       cpu_enable_4_out_3, cpu_enable_5_out_3, logicbitwiseand_1_out_3, multiplexer_1_out,
       n8bitregister_1_out_5, n8bitregister_2_out_5, or_1_out, registerrightlogicshift_1_out_4;

  _8BitRegister u_8bitregister_1 (.in_1(in_2), .s(1'b1), .e(1'b1), .out_5(n8bitregister_1_out_5));  // open: REG
  Multiplexer #(.width(8)) multiplexer_1 (.in0(in_3), .out(multiplexer_1_out), .sel(in_4), .en(1'b1));  // open: in1
  and and_1 (and_1_out, multiplexer_1_out[3], 1'b1);
  _8BitRegister u_8bitregister_2 (.in_1(in_1), .s(1'b1), .e(1'b1), .out_5(n8bitregister_2_out_5));  // open: REG
  CPU_ENABLE cpu_enable_1 (.in_1(n8bitregister_2_out_5), .out_3(cpu_enable_1_out_3), .e(and_1_out));
  registerRightLogicShift registerrightlogicshift_1 (
    .in_1(cpu_enable_1_out_3), .out_4(registerrightlogicshift_1_out_4), .shift_out(in_6), .shift_in(in_7));
  and and_2 (and_2_out, multiplexer_1_out[0], 1'b1);
  and and_3 (and_3_out, multiplexer_1_out[1], multiplexer_1_out[2], 1'b1);
  CPU_ENABLE cpu_enable_2 (.in_1(n8bitregister_2_out_5), .out_3(cpu_enable_2_out_3), .e(and_2_out));
  CPU_ENABLE cpu_enable_3 (.in_1(n8bitregister_1_out_5), .out_3(cpu_enable_3_out_3), .e(and_2_out));
  CPU_ENABLE cpu_enable_4 (.in_1(n8bitregister_2_out_5), .out_3(cpu_enable_4_out_3), .e(and_3_out));
  CPU_ENABLE cpu_enable_5 (.in_1(n8bitregister_1_out_5), .out_3(cpu_enable_5_out_3), .e(and_3_out));
  arithmeticAddition arithmeticaddition_1 (
    .in_1(cpu_enable_2_out_3), .in_2(cpu_enable_3_out_3), .out_5(arithmeticaddition_1_out_5), .carry_in(in_5));  // open: carry_out
  logicBitwiseAND logicbitwiseand_1 (
    .in_1(cpu_enable_4_out_3), .in_2(cpu_enable_5_out_3), .out_3(logicbitwiseand_1_out_3));
  assign or_1_out = arithmeticaddition_1_out_5 | registerrightlogicshift_1_out_4 | logicbitwiseand_1_out_3;  // OR_Gate or_1, 8 bits wide
  _8BitRegister u_8bitregister_3 (.in_1(or_1_out), .s(1'b1), .e(1'b1), .REG(out_8));  // open: out_5

  // Notes on the sheet:
  //   a input
  //   b input
  //   control unit
  //   output
endmodule
